// Logisim project d_flipflop.circ as structural Verilog: 1 circuit, main circuit main
module main (
  input  D,
  input  CLK,
  output Q,
  output NQ
);

  wire nand_1_out, nand_2_out, nand_3_out, nand_4_out, nand_5_out, nand_6_out, nand_7_out, nand_8_out,
       not_1_out;

  not not_1 (not_1_out, CLK);
  nand nand_1 (nand_1_out, D, D);
  nand nand_2 (nand_2_out, D, not_1_out);
  nand nand_3 (nand_3_out, not_1_out, nand_1_out);
  nand nand_4 (nand_4_out, nand_2_out, nand_5_out);
  nand nand_5 (nand_5_out, nand_4_out, nand_3_out);
  nand nand_6 (nand_6_out, nand_4_out, nand_4_out);
  nand nand_7 (nand_7_out, nand_4_out, CLK);
  nand nand_8 (nand_8_out, CLK, nand_6_out);
  nand nand_9 (Q, nand_7_out, NQ);
  nand nand_10 (NQ, Q, nand_8_out);
endmodule
