// Logisim project d_flipflop_sc.circ as structural Verilog: 1 circuit, main circuit main
module main (
  input  D,
  input  CLK,
  input  SET,
  input  CLR,
  output Q,
  output NQ
);

  wire nand_1_out, nand_3_out, nand_4_out, nand_5_out, nand_6_out, nand_7_out, nand_8_out, nand_9_out, nCLR,
       not_1_out, nPRE;

  not not_1 (not_1_out, CLK);
  not not_2 (nCLR, CLR);
  nand nand_1 (nand_1_out, D, D);
  nand nand_2 (nPRE, SET, nCLR);
  nand nand_3 (nand_3_out, D, nCLR, not_1_out);
  nand nand_4 (nand_4_out, not_1_out, nPRE, nand_1_out);
  nand nand_5 (nand_5_out, nand_3_out, nPRE, nand_6_out);
  nand nand_6 (nand_6_out, nand_5_out, nCLR, nand_4_out);
  nand nand_7 (nand_7_out, nand_5_out, nand_5_out);
  nand nand_8 (nand_8_out, nand_5_out, nCLR, CLK);
  nand nand_9 (nand_9_out, CLK, nPRE, nand_7_out);
  nand nand_10 (Q, nand_8_out, nPRE, NQ);
  nand nand_11 (NQ, Q, nCLR, nand_9_out);
endmodule
